// Logisim project better_y86_processor.circ as structural Verilog
module PC_Logic (
  input  [7:0] address_bus,
  input  [4:0] control_in
);

  wire clock_1_out, clock_2_out, comparator_1_eq;
  wire [7:0] adder_1_out, controlled_buffer_1_out, counter_1_q, multiplexer_1_out, PC_q;

  Counter counter_1 (.Q(counter_1_q), .clk(clock_1_out));  // open: load, D, count, carry, clr
  Clock clock_1 (.out(clock_1_out));
  Comparator comparator_1 (.a(counter_1_q), .b(8'ha), .eq(comparator_1_eq));  // open: gt, lt
  assign controlled_buffer_1_out = comparator_1_eq ? 8'h1 : 8'bz;  // Controlled_Buffer controlled_buffer_1
  Register PC (.D(multiplexer_1_out), .Q(PC_q), .clk(clock_2_out));  // open: en, clr
  Clock clock_2 (.out(clock_2_out));
  Adder adder_1 (.a(PC_q), .b(controlled_buffer_1_out), .out(adder_1_out));  // open: cin, cout
  Multiplexer #(.width(8), .enable("false")) multiplexer_1 (
    .in0(adder_1_out), .in1(address_bus), .out(multiplexer_1_out), .sel(control_in[0]));
  // Pins of 1 and 5 bits meet at control_in
endmodule

module ALU (
);

  // Odd_Parity odd_parity_1 is placed but not wired
endmodule
